# Fritzing sketch HydroTrinket (saved by Fritzing 0.9.0b)

parts:
  TRINKET1 = Trinket 5V
  K1 = Relay [part_number=FRS1B-S package=THT]
  K2 = Relay [part_number=FRS1B-S package=THT]

nets:
  N1: TRINKET1.no_name_yet#2, K1.COIL1, K2.COIL1
  N2: TRINKET1.no_name_yet#7, K2.COIL2
  N3: TRINKET1.no_name_yet#8, K1.COIL2
  N4: K1.C1, K1.C2, K2.C1, K2.C2

custom parts:
  Trinket 5V: Adafruit Trinket 5V
